// Logisim project Ctl_Load_Store.circ as structural Verilog: 1 circuit, main circuit Load_Store
module Load_Store (
  input  Enable,
  input  [15:0] Instruction,
  input  Clk,
  input  Reset,
  input  [31:0] Stack_Pointer,
  output PC_Hold,
  output Load,
  output Store,
  output [2:0] Rmd,
  output [31:0] RAM_Addr
);

  wire and_1_out, d_ff_1_q, not_1_out, not_2_out, or_1_out;
  wire [2:0] bit_extender_1_out;
  wire [31:0] adder_1_out, bit_extender_2_out, bit_extender_3_out;

  not not_1 (not_1_out, and_1_out);
  assign bit_extender_1_out = {{2{Enable}}, Enable};  // Bit_Extender bit_extender_1
  assign bit_extender_2_out = {{24{Instruction[7]}}, Instruction[7:0]};  // Bit_Extender bit_extender_2
  and and_1 (and_1_out, Instruction[11], d_ff_1_q);
  D_Flip_Flop d_ff_1 (.D(not_1_out), .clk(Clk), .Q(d_ff_1_q), .reset(or_1_out));  // open: Qn, preset
  or or_1 (or_1_out, ~Enable, ~Instruction[11], Reset);  // OR_Gate
  assign Rmd = Instruction[10:8] & bit_extender_1_out;  // AND_Gate and_2, 3 bits wide
  Adder #(.width(32)) adder_1 (.a(bit_extender_2_out), .b(Stack_Pointer), .out(adder_1_out));  // open: cin, cout
  assign RAM_Addr = adder_1_out & bit_extender_3_out;  // AND_Gate and_3, 32 bits wide
  assign bit_extender_3_out = {{31{Enable}}, Enable};  // Bit_Extender bit_extender_3
  and and_4 (PC_Hold, Enable, and_1_out);
  not not_2 (not_2_out, Instruction[11]);
  and and_5 (Load, Instruction[11], Enable);
  and and_6 (Store, Enable, not_2_out);

  // Other names for the same wires on the sheet: Imm8[7:0] = Instruction[7:0]; DEST[2:0] = Instruction[10:8];
  //   Code = Instruction[11]

  // Notes on the sheet:
  //   Instruction: pull=down
  //   Delay load and hold PC for 1 cycle for the RAM to send out requested data 
endmodule
